# Fritzing sketch Layout (saved by Fritzing 0.9.4)
breadboards: 1

parts:
  Bauteil1 = Arduino Uno (Rev3)
  LED1 = LED - 5mm [color="Red (633nm)" package="5 mm [THT]"]
  LED2 = LED - 5mm [color="Yellow (595nm)" package="5 mm [THT]"]
  LED3 = LED - 5mm [color="Green (570nm)" package="5 mm [THT]"]
  LCD1 = LCD screen
  S2 = Pushbutton [package="[THT]"]
  S3 = Pushbutton [package="[THT]"]
  R1 = Resistor [tolerance=±5% resistance=330 package=THT]
  R2 = Resistor [tolerance=±5% resistance=330 package=THT]
  R3 = Resistor [tolerance=±5% resistance=330 package=THT]
  R4 = Resistor [tolerance=±5% resistance=2.0k package=THT]
  R5 = Resistor [tolerance=±5% resistance=2.0k package=THT]
  Bauteil2 = Adafruit CCS811
  LED4 = LED - 5mm [color="Blue (525nm)" package="5 mm [THT]"]
  R7 = Resistor [tolerance=±5% resistance=330 package=THT]
  microSD1 = MicroSD Card Module
  R8 = Resistor [tolerance=±5% resistance=2.0k package=THT]
  R9 = Resistor [tolerance=±5% resistance=2.0k package=THT]
  S4 = Pushbutton [package="[THT]"]

nets:
  N1: Bauteil1.A2, R1.Pin_0
  N2: Bauteil1.A3, R2.Pin_0
  N3: Bauteil1.A4/SDA, R3.Pin_0, Bauteil2.SDA
  N4: Bauteil1.A5/SCL, Bauteil2.SCL, R7.Pin_0
  N5: Bauteil1.D8, microSD1.CS
  N6: Bauteil1.D9_PWM, microSD1.SCK
  N7: Bauteil1.D10_PWM/SS, microSD1.MOSI
  N8: Bauteil1.D11_PWM/MOSI, microSD1.MISO
  N9: Bauteil1.D12/MISO, S3.Pin_1, S3.Pin_2, R4.Pin_0
  N10: Bauteil1.D13/SCK, S2.Pin_1, S2.Pin_2, R5.Pin_0
  GND: Bauteil1.GND, LED1.anode, LED2.anode, LED3.anode, LCD1.VSS, LCD1.R/W, LCD1.LED-, R4.Pin_1, R5.Pin_1, Bauteil2.GND, Bauteil2.!WAKE, LED4.anode, microSD1.GND, R9.Pin_1
  N11: Bauteil1.AREF, R9.Pin_0, S4.Pin_1, S4.Pin_2
  N12: Bauteil1.D2, LCD1.DB7
  N13: Bauteil1.D3_PWM, LCD1.DB6
  N14: Bauteil1.D4, LCD1.DB5
  N15: Bauteil1.D5_PWM, LCD1.DB4
  N16: Bauteil1.D6_PWM, LCD1.E
  N17: Bauteil1.D7, LCD1.RS
  5V: Bauteil1.5V, LCD1.VDD, LCD1.LED+, S2.Pin_3, S2.Pin_4, S3.Pin_3, S3.Pin_4, microSD1.VCC, R8.Pin_1, S4.Pin_3, S4.Pin_4
  N18: LED1.cathode, R1.Pin_1
  N19: LED2.cathode, R2.Pin_1
  N20: LED3.cathode, R3.Pin_1
  N21: LCD1.V0, R8.Pin_0
  N22: LED4.cathode, R7.Pin_1

notes:
  SD-Modul muss auf den PINs 10 bis 13 sein. Somit müssen zwei Taster sowohl im Layout, als auch im Quellcode auf PINs 8 und 9
